// Logisim project sid_bhatia-cs_11-hw3-circuits_and_ram.circ as structural Verilog: 5 circuits, main circuit SR_Latch
module SR_Latch (
  input  in_1,
  input  in_2,
  output out_3,
  output out_4
);

  wire or_1_out, or_2_out;

  or or_1 (or_1_out, in_1, out_4);
  or or_2 (or_2_out, out_3, in_2);
  not not_1 (out_3, or_1_out);
  not not_2 (out_4, or_2_out);

  // Notes on the sheet:
  //   Provided for you
endmodule

module D_Latch (
  input  in_1,
  input  in_2,
  output out_3
);

  wire and_1_out, and_2_out, not_1_out;

  not not_1 (not_1_out, in_1);
  and and_1 (and_1_out, in_1, in_2);
  and and_2 (and_2_out, not_1_out, in_2);
  SR_Latch SR (.in_1(and_1_out), .in_2(and_2_out), .out_4(out_3));  // open: out_3

  // Notes on the sheet:
  //   Strobe
  //   Provided for you
  //   We ignore the NOT Q output
endmodule

module Decoder (
  input  in_1,
  input  in_2,
  output out_3,
  output out_4,
  output out_5,
  output out_6
);

  wire not_1_out, not_2_out, not_3_out, not_4_out;

  not not_1 (not_1_out, in_1);
  not not_2 (not_2_out, in_2);
  not not_3 (not_3_out, in_1);
  not not_4 (not_4_out, in_2);
  and and_1 (out_3, not_1_out, not_2_out);
  and and_2 (out_4, not_3_out, in_2);
  and and_3 (out_5, in_1, not_4_out);
  and and_4 (out_6, in_1, in_2);

  // Notes on the sheet:
  //   Provided for you
endmodule

module RAM (
  input  in_1,
  input  _2Bit_Addr,
  input  in_3,
  input  _3Bit_Data,
  input  in_5,
  input  in_6,
  output out_7,
  output out_8,
  output out_9
);

  wire and_1_out, and_2_out, and_3_out, and_4_out, and_5_out, and_6_out, and_7_out, and_8_out, and_9_out,
       and_10_out, and_11_out, and_12_out, and_13_out, and_14_out, and_15_out, and_16_out, d_latch_1_out_3,
       d_latch_2_out_3, d_latch_3_out_3, d_latch_4_out_3, d_latch_5_out_3, d_latch_6_out_3, d_latch_7_out_3,
       d_latch_8_out_3, d_latch_9_out_3, d_latch_10_out_3, d_latch_11_out_3, d_latch_12_out_3,
       decoder_1_out_3, decoder_1_out_4, decoder_1_out_5, decoder_1_out_6, undriven, undriven_2, undriven_3,
       undriven_4, undriven_5, undriven_6, undriven_7, undriven_8;

  Decoder decoder_1 (
    .out_4(decoder_1_out_4), .out_6(decoder_1_out_6), .out_5(decoder_1_out_5), .out_3(decoder_1_out_3),
    .in_2(_2Bit_Addr), .in_1(in_1));
  and and_1 (and_1_out, decoder_1_out_3, in_6);
  and and_2 (and_2_out, decoder_1_out_4, in_6);
  and and_3 (and_3_out, decoder_1_out_5, in_6);
  and and_4 (and_4_out, decoder_1_out_6, in_6);
  D_Latch d_latch_1 (.out_3(d_latch_1_out_3), .in_2(and_1_out), .in_1(in_3));
  D_Latch d_latch_2 (.out_3(d_latch_2_out_3), .in_2(and_2_out), .in_1(in_3));
  D_Latch d_latch_3 (.out_3(d_latch_3_out_3), .in_2(and_3_out), .in_1(in_3));
  D_Latch d_latch_4 (.out_3(d_latch_4_out_3), .in_2(and_4_out), .in_1(in_3));
  and and_5 (and_5_out, decoder_1_out_6, decoder_1_out_6, d_latch_4_out_3, undriven);
  and and_6 (and_6_out, undriven, decoder_1_out_5, d_latch_3_out_3, undriven_2);
  and and_7 (and_7_out, undriven_2, decoder_1_out_4, d_latch_2_out_3, undriven_3);
  and and_8 (and_8_out, undriven_3, decoder_1_out_3, d_latch_1_out_3);
  or or_1 (out_8, and_5_out, and_6_out, and_7_out, and_8_out);
  D_Latch d_latch_5 (.out_3(d_latch_5_out_3), .in_2(and_1_out), .in_1(_3Bit_Data));
  D_Latch d_latch_6 (.out_3(d_latch_6_out_3), .in_2(and_2_out), .in_1(_3Bit_Data));
  D_Latch d_latch_7 (.out_3(d_latch_7_out_3), .in_2(and_3_out), .in_1(_3Bit_Data));
  D_Latch d_latch_8 (.out_3(d_latch_8_out_3), .in_2(and_4_out), .in_1(_3Bit_Data));
  and and_9 (and_9_out, decoder_1_out_6, d_latch_8_out_3, undriven_4);
  and and_10 (and_10_out, undriven_4, decoder_1_out_5, d_latch_7_out_3, undriven_5);
  and and_11 (and_11_out, undriven_5, decoder_1_out_4, d_latch_6_out_3, undriven_6);
  or or_2 (out_9, and_9_out, and_10_out, and_11_out, and_12_out);
  and and_12 (and_12_out, undriven_6, decoder_1_out_3, d_latch_5_out_3);
  D_Latch d_latch_9 (.out_3(d_latch_9_out_3), .in_2(and_1_out), .in_1(in_5));
  D_Latch d_latch_10 (.out_3(d_latch_10_out_3), .in_2(and_2_out), .in_1(in_5));
  D_Latch d_latch_11 (.out_3(d_latch_11_out_3), .in_2(and_3_out), .in_1(in_5));
  D_Latch d_latch_12 (.out_3(d_latch_12_out_3), .in_2(and_4_out), .in_1(in_5));
  and and_13 (and_13_out, d_latch_12_out_3, decoder_1_out_6, decoder_1_out_5);
  and and_14 (and_14_out, undriven_7, decoder_1_out_4, d_latch_10_out_3, undriven_8);
  and and_15 (and_15_out, decoder_1_out_6, decoder_1_out_5, d_latch_11_out_3, undriven_7);
  or or_3 (out_7, and_13_out, and_15_out, and_14_out, and_16_out);
  and and_16 (and_16_out, undriven_8, decoder_1_out_3, d_latch_9_out_3);

  // Notes on the sheet:
  //   Write 
  //   Name:
  //   Sid Bhatia
  //   Pledge:
  //   Implement  3 Bit, 4 Word RAM
  //   Implement the WRITE operation
  //   I pledge my honor that I have abided by the Stevens Honor System.
  //   The 3 Bit Output should reflect the values stored in the word selected by the 2Bit Addr
  //   If you need help, look at slides 9-16 in week9.pdf
  //   3 Bit Out
endmodule

module remain (
  input  in_1,
  input  in_2,
  input  in_3,
  input  in_4,
  input  in_5,
  output out_6,
  output out_7,
  output out_8
);

  wire and_1_out, and_2_out, and_3_out, and_4_out, and_5_out, and_6_out, and_7_out, and_8_out, not_2_out,
       not_4_out, not_5_out, not_6_out, or2_out, or_1_out, or_2_out;

  // NOT_Gate not_1 has open pins: in=in_1, out=open
  and and_1 (and_1_out, in_1, in_2);
  and and_2 (and_2_out, and_1_out, or2_out);
  not not_2 (not_2_out, in_2);
  or or_1 (or_1_out, in_1, in_2);
  not not_3 (out_6, or_1_out);
  and and2 (out_7, and_1_out, or_2_out);
  and and_3 (and_3_out, in_1, not_2_out, in_5);
  not not_4 (not_4_out, in_3);
  and and_4 (and_4_out, not_4_out, not_5_out, in_5);
  or or1 (out_8, and_3_out, and_2_out);
  not not_5 (not_5_out, in_4);
  and and_5 (and_5_out, in_3, in_4, in_5);
  or or2 (or2_out, and_5_out, and_7_out, and_4_out);
  not not_6 (not_6_out, in_5);
  and and_6 (and_6_out, in_3, not_5_out, in_5);
  and and_7 (and_7_out, in_3, not_5_out, not_6_out);
  and and_8 (and_8_out, not_4_out, in_4, not_6_out);
  or or_2 (or_2_out, and_8_out, and_6_out);

  // Notes on the sheet:
  //   and 1
  //   divisor 
  //   Error bit (Set when division isn't possible)
  //   numerator
  //   Remainder
  //   or3
endmodule
