// Logisim project sid_bhatia-lab8-parity.circ as structural Verilog: 2 circuits, main circuit ParityGenerator
module XOR (
  input  X,
  input  Y,
  output out_3
);


  // Notes on the sheet:
  //   Use minterm expansion to create an XOR gate using AND + OR gates
endmodule

module ParityGenerator (
  input  X,
  input  Y,
  input  Z,
  output Parity
);

  wire not_1_out, not_2_out, not_3_out;

  not not_1 (not_1_out, X);
  // AND_Gate and_1 has open pins: in0=not_1_out, in1=Y, out=open
  // AND_Gate and_2 has open pins: in0=not_1_out, in1=not_2_out, out=open
  // NOT_Gate not_2 has open pins: in=open, out=not_2_out
  // AND_Gate and_3 is placed but not wired
  // NOT_Gate not_3 has open pins: in=open, out=not_3_out
  // AND_Gate and_4 has open pins: in0=not_2_out, in1=not_3_out, in2=X, out=open

  // Notes on the sheet:
  //   Input Bits
  //   Output Bit
  //   Write your parity circuit here
  //   the output = 1 if an odd number of inputs (1 or 3) are 1, otherwise 0
  //   ONLY use: NOT, AND, OR, and any custom functions you write (included in the .circ submission)
  //   WRITE YOUR NAME AND PLEDGE SOMEWHERE IN THIS CIRCUIT
  //   Siddharth Bhatia
  //   I pledge my honor that I have abided by the Stevens Honor System.
  //   f(x,y,z) = \bar[x]\bar[y]\bar[z] + \bar[x]\bar[y]z + \bar[x]y\bar[z] + x\bar[y]\bar[z] + xyz
  //   x, y, z | f(x,y,z)
  //   0 0 0 |       1
  //   0 0 1 |       1
  //   0 1 0 |       1
  //   1 0 0 |       1
  //   0 1 1 |       0
  //   1 0 1 |        0
  //   1 1 1 |        1
endmodule
